# Fritzing sketch wiring_v1 (saved by Fritzing 1.0.3b)
# 18650 Li-ion Battery: CC-BY Dr Kristofer Chan, King's College London/Remote-research.org

parts:
  Part1 = Arduino Uno (Rev3) - ICSP
  M1 = gear-motor
  M2 = gear-motor
  S2 = H-Bridge with L298N
  BAT1 = 18650 Li-ion Battery [package=battery-18650]
  BAT2 = 18650 Li-ion Battery [package=battery-18650]
  U2 = SWITCH-SPST-2 [package=switch-spst-vertical]
  M3 = gear-motor  # not connected
  M4 = gear-motor  # not connected
  M5 = gear-motor
  S3 = H-Bridge with L298N

nets:
  N1: Part1.D9_PWM, S2.IN4
  N2: Part1.D10_PWM/SS, S2.IN3
  N3: Part1.D5_PWM, S2.IN2
  N4: Part1.D6_PWM, S2.IN1
  N5: Part1.VIN, U2.P
  N6: M1.pin_1, S2.M2-02
  N7: M1.pin_2, S2.M2-01
  N8: M2.pin_1, S2.M1-02
  N9: M2.pin_2, S2.M1-01
  N10: S2.GND, BAT1.-
  N11: BAT1.+, BAT2.-
  N12: BAT2.+, U2.O
  N13: M5.pin_1, S3.M1-02
  N14: M5.pin_2, S3.M1-01

custom parts:
  H-Bridge with L298N: h-bridge
  18650 Li-ion Battery: 18650 li-ion Battery Standard 18650 battery with interactive connectors Creative Common Attribution 4.0 International (CC-BY 4.0) license. Any use of this part requires attribution of Dr Kristofer Chan, Department of Geography, King's College London. Contact kristofer.chan [at] kcl.ac.uk OR kris [at] remote-research.org for further information.
